# Fritzing sketch Esquema-de-conexion (saved by Fritzing 0.9.3b)
breadboards: 1

parts:
  Componente1 = Arduino Uno (Rev3)
  U3 = HC-SR04 [chip_label=IC package="SIP (Single Inline) [THT]"]
  LED1 = smd LED [color="White (6500K)" package="0603 [SMD]"]

nets:
  N1: Componente1.D8, LED1.cathode
  N2: Componente1.D6_PWM, U3.Echo
  N3: Componente1.D7, U3.Trig
  5V: Componente1.5V, U3.Vcc
  GND: Componente1.GND, U3.GND, LED1.anode

custom parts:
  HC-SR04: HC-SR04 ultrasound distance sensor
